// Logisim project ALU_template.circ as structural Verilog: 17 circuits, main circuit ALU32
module LeftShift32 (
  input  [31:0] B,
  input  [4:0] Sa,
  input  Cin,
  output [31:0] C
);

  wire [31:0] eightshifter_1_c, fourshifter_1_c, multiplexer_1_out, multiplexer_2_out, multiplexer_3_out,
       multiplexer_4_out, oneshifter_1_c, sixteenshifter_1_c, twoshifter_1_c;

  OneShifter oneshifter_1 (.Cin(Cin), .B(B), .C(oneshifter_1_c));
  Multiplexer #(.width(32), .enable("false")) multiplexer_1 (
    .in0(B), .in1(oneshifter_1_c), .out(multiplexer_1_out), .sel(Sa[0]));
  TwoShifter twoshifter_1 (.Cin(Cin), .B(multiplexer_1_out), .C(twoshifter_1_c));
  Multiplexer #(.width(32), .enable("false")) multiplexer_2 (
    .in0(multiplexer_1_out), .in1(twoshifter_1_c), .out(multiplexer_2_out), .sel(Sa[1]));
  FourShifter fourshifter_1 (.Cin(Cin), .B(multiplexer_2_out), .C(fourshifter_1_c));
  Multiplexer #(.width(32), .enable("false")) multiplexer_3 (
    .in0(multiplexer_2_out), .in1(fourshifter_1_c), .out(multiplexer_3_out), .sel(Sa[2]));
  EightShifter eightshifter_1 (.Cin(Cin), .B(multiplexer_3_out), .C(eightshifter_1_c));
  Multiplexer #(.width(32), .enable("false")) multiplexer_4 (
    .in0(multiplexer_3_out), .in1(eightshifter_1_c), .out(multiplexer_4_out), .sel(Sa[3]));
  SixteenShifter sixteenshifter_1 (.Cin(Cin), .B(multiplexer_4_out), .C(sixteenshifter_1_c));
  Multiplexer #(.width(32), .enable("false")) multiplexer_5 (
    .in0(multiplexer_4_out), .in1(sixteenshifter_1_c), .out(C), .sel(Sa[4]));
endmodule

module Add32 (
  input  [31:0] A,
  input  [31:0] B,
  input  Cin,
  output V,
  output [31:0] C
);

  wire eightbitadder_1_cout, fourbitadder_1_cout, onebitadder_1_cout, onebitadder_2_cout,
       sixteenbitadder_1_cout, twobitadder_1_cout;

  SixteenBitAdder sixteenbitadder_1 (
    .A(A[15:0]), .B(B[15:0]), .Cin(Cin), .Cout(sixteenbitadder_1_cout), .C(C[15:0]));  // open: V
  EightBitAdder eightbitadder_1 (
    .A(A[23:16]), .B(B[23:16]), .Cin(sixteenbitadder_1_cout), .Cout(eightbitadder_1_cout), .C(C[23:16]));  // open: V
  FourBitAdder fourbitadder_1 (
    .A(A[27:24]), .B(B[27:24]), .Cin(eightbitadder_1_cout), .Cout(fourbitadder_1_cout), .C(C[27:24]));  // open: V
  TwoBitAdder twobitadder_1 (
    .A(A[29:28]), .B(B[29:28]), .Cin(fourbitadder_1_cout), .Cout(twobitadder_1_cout), .C(C[29:28]));  // open: V
  OneBitAdder onebitadder_1 (.A(A[30]), .B(B[30]), .Cin(twobitadder_1_cout), .C(C[30]), .Cout(onebitadder_1_cout));
  OneBitAdder onebitadder_2 (.A(A[31]), .B(B[31]), .Cin(onebitadder_1_cout), .C(C[31]), .Cout(onebitadder_2_cout));
  xor xor_1 (V, onebitadder_2_cout, onebitadder_1_cout);
endmodule

module ALU32 (
  input  [31:0] A,
  input  [31:0] B,
  input  [3:0] Op,
  input  [4:0] Sa,
  output [31:0] C,
  output V
);

  wire and_1_out, arithmetic_1_v, not_1_out;
  wire [31:0] arithmetic_1_c, comparable_1_c, logicgates_1_c, multiplexer_1_out, multiplexer_2_out,
       shifters_1_c;

  Shifters shifters_1 (.B(B), .Sa(Sa), .S({Op[2], Op[0]}), .C(shifters_1_c));
  LogicGates logicgates_1 (.A(A), .B(B), .S(Op[2:1]), .C(logicgates_1_c));
  Comparable comparable_1 (.A(A), .B(B), .S(Op[2:1]), .C(comparable_1_c));
  Arithmetic arithmetic_1 (.A(A), .B(B), .S(Op[2]), .V(arithmetic_1_v), .C(arithmetic_1_c));
  Multiplexer #(.width(32), .enable("false")) multiplexer_1 (
    .in0(comparable_1_c), .in1(logicgates_1_c), .out(multiplexer_1_out), .sel(Op[0]));
  Multiplexer #(.width(32), .enable("false")) multiplexer_2 (
    .in0(arithmetic_1_c), .in1(shifters_1_c), .out(multiplexer_2_out), .sel(Op[1]));
  Multiplexer #(.width(32), .enable("false")) multiplexer_3 (
    .in0(multiplexer_1_out), .in1(multiplexer_2_out), .out(C), .sel(Op[3]));
  not not_1 (not_1_out, Op[1]);
  and and_1 (and_1_out, not_1_out, Op[3]);
  and and_2 (V, arithmetic_1_v, and_1_out);
endmodule

module OneShifter (
  input  Cin,
  input  [31:0] B,
  output [31:0] C
);


  assign C = {B[30:0], Cin};
endmodule

module TwoShifter (
  input  Cin,
  input  [31:0] B,
  output [31:0] C
);

  wire [31:0] oneshifter_1_c;

  OneShifter oneshifter_1 (.Cin(Cin), .B(B), .C(oneshifter_1_c));
  OneShifter oneshifter_2 (.Cin(Cin), .B(oneshifter_1_c), .C(C));
endmodule

module FourShifter (
  input  Cin,
  input  [31:0] B,
  output [31:0] C
);

  wire [31:0] twoshifter_1_c;

  TwoShifter twoshifter_1 (.Cin(Cin), .B(B), .C(twoshifter_1_c));
  TwoShifter twoshifter_2 (.Cin(Cin), .B(twoshifter_1_c), .C(C));
endmodule

module EightShifter (
  input  Cin,
  input  [31:0] B,
  output [31:0] C
);

  wire [31:0] fourshifter_1_c;

  FourShifter fourshifter_1 (.Cin(Cin), .B(B), .C(fourshifter_1_c));
  FourShifter fourshifter_2 (.Cin(Cin), .B(fourshifter_1_c), .C(C));
endmodule

module SixteenShifter (
  input  Cin,
  input  [31:0] B,
  output [31:0] C
);

  wire [31:0] eightshifter_1_c;

  EightShifter eightshifter_1 (.Cin(Cin), .B(B), .C(eightshifter_1_c));
  EightShifter eightshifter_2 (.Cin(Cin), .B(eightshifter_1_c), .C(C));
endmodule

module OneBitAdder (
  input  A,
  input  B,
  input  Cin,
  output C,
  output Cout
);

  wire and_1_out, and_2_out, xor_1_out;

  xor xor_1 (xor_1_out, A, B);
  xor xor_2 (C, xor_1_out, Cin);
  and and_1 (and_1_out, xor_1_out, Cin);
  and and_2 (and_2_out, A, B);
  or or_1 (Cout, and_1_out, and_2_out);
endmodule

module TwoBitAdder (
  input  [1:0] A,
  input  [1:0] B,
  input  Cin,
  output Cout,
  output V,
  output [1:0] C
);

  wire onebitadder_1_cout;

  OneBitAdder onebitadder_1 (.A(A[0]), .B(B[0]), .Cin(Cin), .C(C[0]), .Cout(onebitadder_1_cout));
  OneBitAdder onebitadder_2 (.A(A[1]), .B(B[1]), .Cin(onebitadder_1_cout), .C(C[1]), .Cout(Cout));
  xor xor_1 (V, Cout, onebitadder_1_cout);
endmodule

module FourBitAdder (
  input  [3:0] A,
  input  [3:0] B,
  input  Cin,
  output Cout,
  output V,
  output [3:0] C
);

  wire onebitadder_1_cout, twobitadder_1_cout;

  TwoBitAdder twobitadder_1 (.A(A[1:0]), .B(B[1:0]), .Cin(Cin), .Cout(twobitadder_1_cout), .C(C[1:0]));  // open: V
  OneBitAdder onebitadder_1 (.A(A[2]), .B(B[2]), .Cin(twobitadder_1_cout), .C(C[2]), .Cout(onebitadder_1_cout));
  OneBitAdder onebitadder_2 (.A(A[3]), .B(B[3]), .Cin(onebitadder_1_cout), .C(C[3]), .Cout(Cout));
  xor xor_1 (V, Cout, onebitadder_1_cout);
endmodule

module EightBitAdder (
  input  [7:0] A,
  input  [7:0] B,
  input  Cin,
  output Cout,
  output V,
  output [7:0] C
);

  wire fourbitadder_1_cout, onebitadder_1_cout, twobitadder_1_cout;

  FourBitAdder fourbitadder_1 (.A(A[3:0]), .B(B[3:0]), .Cin(Cin), .Cout(fourbitadder_1_cout), .C(C[3:0]));  // open: V
  TwoBitAdder twobitadder_1 (
    .A(A[5:4]), .B(B[5:4]), .Cin(fourbitadder_1_cout), .Cout(twobitadder_1_cout), .C(C[5:4]));  // open: V
  OneBitAdder onebitadder_1 (.A(A[6]), .B(B[6]), .Cin(twobitadder_1_cout), .C(C[6]), .Cout(onebitadder_1_cout));
  OneBitAdder onebitadder_2 (.A(A[7]), .B(B[7]), .Cin(onebitadder_1_cout), .C(C[7]), .Cout(Cout));
  xor xor_1 (V, Cout, onebitadder_1_cout);
endmodule

module SixteenBitAdder (
  input  [15:0] A,
  input  [15:0] B,
  input  Cin,
  output Cout,
  output V,
  output [15:0] C
);

  wire eightbitadder_1_cout, fourbitadder_1_cout, onebitadder_1_cout, twobitadder_1_cout;

  EightBitAdder eightbitadder_1 (
    .A(A[7:0]), .B(B[7:0]), .Cin(Cin), .Cout(eightbitadder_1_cout), .C(C[7:0]));  // open: V
  FourBitAdder fourbitadder_1 (
    .A(A[11:8]), .B(B[11:8]), .Cin(eightbitadder_1_cout), .Cout(fourbitadder_1_cout), .C(C[11:8]));  // open: V
  TwoBitAdder twobitadder_1 (
    .A(A[13:12]), .B(B[13:12]), .Cin(fourbitadder_1_cout), .Cout(twobitadder_1_cout), .C(C[13:12]));  // open: V
  OneBitAdder onebitadder_1 (.A(A[14]), .B(B[14]), .Cin(twobitadder_1_cout), .C(C[14]), .Cout(onebitadder_1_cout));
  OneBitAdder onebitadder_2 (.A(A[15]), .B(B[15]), .Cin(onebitadder_1_cout), .C(C[15]), .Cout(Cout));
  xor xor_1 (V, Cout, onebitadder_1_cout);
endmodule

module LogicGates (
  input  [31:0] A,
  input  [31:0] B,
  input  [1:0] S,
  output [31:0] C
);

  wire [31:0] and_1_out, nor_1_out, or_1_out, xor_1_out;

  assign or_1_out = A | B;  // OR_Gate or_1, 32 bits wide
  assign and_1_out = A & B;  // AND_Gate and_1, 32 bits wide
  assign nor_1_out = ~(A | B);  // NOR_Gate nor_1, 32 bits wide
  assign xor_1_out = A ^ B;  // XOR_Gate xor_1, 32 bits wide
  Multiplexer #(.select(2), .width(32), .enable("false")) multiplexer_1 (
    .in0(or_1_out), .in1(and_1_out), .in2(nor_1_out), .in3(xor_1_out), .out(C), .sel(S));
endmodule

module Comparable (
  input  [31:0] A,
  input  [31:0] B,
  input  [1:0] S,
  output [31:0] C
);

  wire and_1_out, nor_1_out, not_1_out, not_2_out, or_1_out;
  wire [31:0] xnor_1_out;

  nor nor_1 (nor_1_out, A[30], A[29], A[28], A[27], A[26], A[25], A[24], A[23], A[22], A[21], A[20], A[19], A[18], A[17], A[16], A[15], A[14], A[13], A[12], A[11], A[10], A[9], A[8], A[7], A[6], A[5], A[4], A[3], A[2], A[1], A[0]);
  or or_1 (or_1_out, nor_1_out, A[31]);
  assign xnor_1_out = ~(A ^ B);  // XNOR_Gate xnor_1, 32 bits wide
  not not_1 (not_1_out, or_1_out);
  and and_1 (and_1_out, xnor_1_out[0], xnor_1_out[1], xnor_1_out[2], xnor_1_out[3], xnor_1_out[4], xnor_1_out[5], xnor_1_out[6], xnor_1_out[7], xnor_1_out[8], xnor_1_out[9], xnor_1_out[10], xnor_1_out[11], xnor_1_out[12], xnor_1_out[13], xnor_1_out[14], xnor_1_out[15], xnor_1_out[16], xnor_1_out[17], xnor_1_out[18], xnor_1_out[19], xnor_1_out[20], xnor_1_out[21], xnor_1_out[22], xnor_1_out[23], xnor_1_out[24], xnor_1_out[25], xnor_1_out[26], xnor_1_out[27], xnor_1_out[28], xnor_1_out[29], xnor_1_out[30], xnor_1_out[31]);
  not not_2 (not_2_out, and_1_out);
  Multiplexer #(.select(2), .enable("false")) multiplexer_1 (
    .in0(not_2_out), .in1(and_1_out), .in2(or_1_out), .in3(not_1_out), .out(C[0]), .sel(S));
  assign C[31:1] = {{30{1'b0}}, 1'b0};  // Bit_Extender bit_extender_1
endmodule

module Arithmetic (
  input  [31:0] A,
  input  [31:0] B,
  input  S,
  output V,
  output [31:0] C
);

  wire [31:0] bit_extender_1_out, xor_1_out;

  assign bit_extender_1_out = {{31{S}}, S};  // Bit_Extender bit_extender_1
  assign xor_1_out = B ^ bit_extender_1_out;  // XOR_Gate xor_1, 32 bits wide
  Add32 add32_1 (.A(A), .B(xor_1_out), .Cin(S), .V(V), .C(C));
endmodule

module Shifters (
  input  [31:0] B,
  input  [4:0] Sa,
  input  [1:0] S,
  output [31:0] C
);

  wire and_1_out, and_2_out;
  wire [31:0] leftshift32_1_c, multiplexer_1_out;

  and and_1 (and_1_out, B[31], and_2_out);
  and and_2 (and_2_out, S[0], S[1]);
  Multiplexer #(.width(32), .enable("false")) multiplexer_1 (
    .in0(B),
    .in1({B[0], B[1], B[2], B[3], B[4], B[5], B[6], B[7], B[8], B[9], B[10], B[11], B[12], B[13], B[14], B[15], B[16], B[17], B[18], B[19], B[20], B[21], B[22], B[23], B[24], B[25], B[26], B[27], B[28], B[29], B[30], B[31]}),
    .out(multiplexer_1_out), .sel(S[1]));
  LeftShift32 leftshift32_1 (.B(multiplexer_1_out), .Sa(Sa), .Cin(and_1_out), .C(leftshift32_1_c));
  Multiplexer #(.width(32), .enable("false")) multiplexer_2 (
    .in0(leftshift32_1_c),
    .in1({leftshift32_1_c[0], leftshift32_1_c[1], leftshift32_1_c[2], leftshift32_1_c[3], leftshift32_1_c[4], leftshift32_1_c[5], leftshift32_1_c[6], leftshift32_1_c[7], leftshift32_1_c[8], leftshift32_1_c[9], leftshift32_1_c[10], leftshift32_1_c[11], leftshift32_1_c[12], leftshift32_1_c[13], leftshift32_1_c[14], leftshift32_1_c[15], leftshift32_1_c[16], leftshift32_1_c[17], leftshift32_1_c[18], leftshift32_1_c[19], leftshift32_1_c[20], leftshift32_1_c[21], leftshift32_1_c[22], leftshift32_1_c[23], leftshift32_1_c[24], leftshift32_1_c[25], leftshift32_1_c[26], leftshift32_1_c[27], leftshift32_1_c[28], leftshift32_1_c[29], leftshift32_1_c[30], leftshift32_1_c[31]}),
    .out(C), .sel(S[1]));
endmodule
