// Logisim project pipeline.circ as structural Verilog: 8 circuits, main circuit RISCV
module RISCV (
);

  wire clock_1_out;
  wire [4:0] decode_1_ra, decode_1_rb, execute_1_rd, Ra_q, Rb_q, Rd_q, registerfile_1_p3;
  wire [12:0] ctrl_q, decode_1_ctrl;
  wire [29:0] incrementer_1_p2;
  wire [31:0] A_q, auipc_q, B_q, D_q, decode_1_imm, execute_1_d, hazard_1_resa, hazard_1_resb, imm_q,
       incrementer_1_p1, inst_q, registerfile_1_p1, registerfile_1_p6, registerfile_1_p7,
       risc_vprogramrom_1_p2;

  Clock clock_1 (.out(clock_1_out));
  // Incrementer #(.width(30)) incrementer_1: pin names not known; wires that end beside it: incrementer_1_p1[31:2], incrementer_1_p2
  // RISC_VProgramROM risc_vprogramrom_1: pin names not known; wires that end beside it: incrementer_1_p1, risc_vprogramrom_1_p2
  Register #(.width(32)) PC (
    .D({incrementer_1_p2, incrementer_1_p1[1:0]}), .clk(clock_1_out), .Q(incrementer_1_p1));  // open: en, clr
  Register #(.width(32)) inst (.D(risc_vprogramrom_1_p2), .clk(clock_1_out), .Q(inst_q));  // open: en, clr
  Register #(.width(32)) auipc (.D(incrementer_1_p1), .clk(clock_1_out), .Q(auipc_q));  // open: en, clr
  Decode decode_1 (
    .PC(auipc_q), .Inst(inst_q), .Ra(decode_1_ra), .Rb(decode_1_rb), .Imm(decode_1_imm), .ctrl(decode_1_ctrl));
  // RegisterFile #(.trigger("falling")) registerfile_1: pin names not known; wires that end beside it: registerfile_1_p1, clock_1_out, registerfile_1_p3, decode_1_ra, decode_1_rb, registerfile_1_p6, registerfile_1_p7
  Register #(.width(5)) Ra (.D(decode_1_ra), .clk(clock_1_out), .Q(Ra_q));  // open: en, clr
  Register #(.width(5)) Rb (.D(decode_1_rb), .clk(clock_1_out), .Q(Rb_q));  // open: en, clr
  Register #(.width(32)) A (.D(registerfile_1_p6), .clk(clock_1_out), .Q(A_q));  // open: en, clr
  Register #(.width(32)) B (.D(registerfile_1_p7), .clk(clock_1_out), .Q(B_q));  // open: en, clr
  Register #(.width(32)) imm (.D(decode_1_imm), .clk(clock_1_out), .Q(imm_q));  // open: en, clr
  Register #(.width(13)) ctrl (.D(decode_1_ctrl), .clk(clock_1_out), .Q(ctrl_q));  // open: en, clr
  Hazard hazard_1 (
    .Mem_value(D_q), .Ra(Ra_q), .Rb(Rb_q), .R_mem(Rd_q), .A_value(A_q), .B_value(B_q),
    .Write_value(registerfile_1_p1), .R_write(registerfile_1_p3), .resA(hazard_1_resa), .resB(hazard_1_resb));
  Register #(.width(32)) D (.D(execute_1_d), .clk(clock_1_out), .Q(D_q));  // open: en, clr
  Execute execute_1 (
    .A(hazard_1_resa), .imm(imm_q), .B(hazard_1_resb), .ctrl(ctrl_q), .D(execute_1_d), .Rd(execute_1_rd));
  Register #(.width(5)) Rd (.D(execute_1_rd), .clk(clock_1_out), .Q(Rd_q));  // open: en, clr
  Register #(.width(32)) D2 (.D(D_q), .clk(clock_1_out), .Q(registerfile_1_p1));  // open: en, clr
  Register #(.width(5)) Rd2 (.D(Rd_q), .clk(clock_1_out), .Q(registerfile_1_p3));  // open: en, clr

  // Notes on the sheet:
  //   contents of risc_vprogramrom_1 (hex, n*v repeats v):
  //   addi x2, x2, 2 addi x3, x3, 3 addi x4, x4, 31 add x6, x1, x2 sub x7, x2, x1 sub x5, x1, x3 and x8,
  //   x3, x2 andi x9, x2, 6 or x10, x4, x3 ori x11, x3, 8 xor x12, x3, x1 xori x13, x3, 7 slt x14, x1, x2
  //   slti x15, x5, 5 sltu x16, x1, x2 sltiu x17, x5, 5 sra x18, x5, x4 srai x19, x4, 1 srl x20, x4, x1
  //   srli x21, x4, 2 sll x22, x4, x1 slli x23, x4, 2 lui x24, 20 auipc x25, 20
endmodule

module Decode (
  input  [31:0] PC,
  input  [31:0] Inst,
  output [4:0] Ra,
  output [4:0] Rb,
  output [31:0] Imm,
  output [12:0] ctrl
);

  wire not_1_out, not_2_out, not_3_out, or_1_out, secondbit_1_res, srlcheck_1_res, xorcheck_1_res;
  wire [2:0] xor_1_out;
  wire [4:0] bit_extender_1_out;
  wire [31:0] adder_1_out, bit_extender_2_out, bit_extender_3_out, multiplexer_1_out;

  assign bit_extender_1_out = {{4{Inst[4]}}, Inst[4]};  // Bit_Extender bit_extender_1
  assign bit_extender_2_out = {{20{Inst[31]}}, Inst[31:20]};  // Bit_Extender bit_extender_2
  assign bit_extender_3_out = {{12{1'b0}}, Inst[31:12]};  // Bit_Extender bit_extender_3
  not not_1 (not_1_out, Inst[2]);
  or or_1 (or_1_out, not_1_out, Inst[5]);
  not not_2 (not_2_out, Inst[13]);
  Multiplexer #(.width(32), .enable("false")) multiplexer_1 (
    .in0(bit_extender_2_out), .in1({bit_extender_3_out[19:0], bit_extender_3_out[31:20]}),
    .out(multiplexer_1_out), .sel(Inst[2]));
  assign ctrl[8:4] = bit_extender_1_out & Inst[11:7];  // AND_Gate and_1, 5 bits wide
  xorCheck xorcheck_1 (.inp(Inst[14:12]), .res(xorcheck_1_res));
  srlCheck srlcheck_1 (.inp({Inst[30], Inst[14:12]}), .res(srlcheck_1_res));
  secondBit secondbit_1 (.inp({Inst[30], Inst[14:12]}), .I_or_R(Inst[5]), .res(secondbit_1_res));
  xor xor_1 (xor_1_out[0], Inst[12], xorcheck_1_res);
  xor xor_2 (xor_1_out[2], not_2_out, xorcheck_1_res);
  or or_2 (xor_1_out[1], xorcheck_1_res, srlcheck_1_res, secondbit_1_res);
  Adder #(.width(32)) adder_1 (.a(multiplexer_1_out), .b(PC), .out(adder_1_out));  // open: cin, cout
  not not_3 (not_3_out, srlcheck_1_res);
  otherInstr otherinstr_1 (.Inst(Inst), .res(ctrl[12:10]));
  assign {ctrl[0], ctrl[3:1]} = {{1{not_3_out}}, xor_1_out};  // Bit_Extender bit_extender_4
  Multiplexer #(.width(32), .enable("false")) multiplexer_2 (
    .in0(adder_1_out), .in1(multiplexer_1_out), .out(Imm), .sel(or_1_out));

  assign ctrl[9] = Inst[5];
  assign Ra = Inst[19:15];
  assign Rb = Inst[24:20];

  // Notes on the sheet:
  //   Rd
  //   funct3
  //   funct7
  //   5 bit Rd
  //   0 if nonfunctional instruction
  //   4 bit Op for ALU
endmodule

module xorCheck (
  input  [2:0] inp,
  output res
);

  wire not_1_out;

  not not_1 (not_1_out, inp[2]);
  nor nor_1 (res, inp[0], inp[1], not_1_out);

  // Notes on the sheet:
  //   outputs 1 iff inp corresponds to XOR
endmodule

module srlCheck (
  input  [3:0] inp,
  output res
);

  wire not_1_out, not_2_out;

  not not_1 (not_1_out, inp[1]);
  not not_2 (not_2_out, inp[3]);
  and and_1 (res, inp[0], not_1_out, inp[2], not_2_out);

  // Notes on the sheet:
  //   outputs 1 iff inp corresponds to SRL
endmodule

module otherInstr (
  input  [31:0] Inst,
  output [2:0] res
);

  wire and_1_out, not_1_out, not_2_out;

  not not_1 (not_1_out, Inst[12]);
  not not_2 (not_2_out, Inst[14]);
  and and_1 (and_1_out, not_1_out, Inst[13], not_2_out);
  and and_2 (res[2], Inst[12], Inst[13], not_2_out);
  or or_1 (res[1], and_1_out, res[2]);

  assign res[0] = Inst[2];

  // Notes on the sheet:
  //   0th bit is 1 iff U type instruction
  //   1st bit is 1 iff comparison instruction
  //   If comparison inst, 2nd bit is 1 iff SLTU or SLTIU
endmodule

module Execute (
  input  [31:0] A,
  input  [31:0] imm,
  input  [31:0] B,
  input  [12:0] ctrl,
  output [31:0] D,
  output [4:0] Rd
);

  wire comparator_1_lt, not_1_out, not_2_out;
  wire [4:0] alu_1_p4;
  wire [31:0] alu_1_p5, bit_extender_2_out, multiplexer_1_out, multiplexer_2_out;
  wire [31:31] xor_1_out, xor_2_out;

  Multiplexer #(.width(32), .enable("false")) multiplexer_1 (
    .in0(imm), .in1(B), .out(multiplexer_1_out), .sel(ctrl[9]));
  not not_1 (not_1_out, ctrl[12]);
  not not_2 (not_2_out, ctrl[12]);
  xor xor_1 (xor_1_out[31], A[31], not_1_out);
  xor xor_2 (xor_2_out[31], multiplexer_1_out[31], not_2_out);
  Comparator #(.width(32), .mode("unsigned")) comparator_1 (
    .a({xor_1_out[31], A[30:0]}), .b({xor_2_out[31], multiplexer_1_out[30:0]}), .lt(comparator_1_lt));  // open: gt, eq
  // ALU alu_1: pin names not known; wires that end beside it: A, multiplexer_1_out, ctrl[3:0], alu_1_p4, alu_1_p5
  Bit_Extender #(.in_width(32), .out_width(5)) bit_extender_1 (.in(imm), .out(alu_1_p4));
  assign bit_extender_2_out = {{31{1'b0}}, comparator_1_lt};  // Bit_Extender bit_extender_2
  Multiplexer #(.width(32), .enable("false")) multiplexer_2 (
    .in0(alu_1_p5), .in1(bit_extender_2_out), .out(multiplexer_2_out), .sel(ctrl[11]));
  Multiplexer #(.width(32), .enable("false")) multiplexer_3 (
    .in0(multiplexer_2_out), .in1(imm), .out(D), .sel(ctrl[10]));

  assign Rd = ctrl[8:4];
endmodule

module Hazard (
  input  [31:0] Mem_value,
  input  [4:0] Ra,
  input  [4:0] Rb,
  input  [4:0] R_mem,
  input  [31:0] A_value,
  input  [31:0] B_value,
  input  [31:0] Write_value,
  input  [4:0] R_write,
  output [31:0] resA,
  output [31:0] resB
);

  wire and_1_out, and_2_out, and_3_out, and_4_out, or_1_out, or_2_out, or_3_out, or_4_out;
  wire [4:0] xnor_1_out, xnor_2_out, xnor_3_out, xnor_4_out;
  wire [31:0] multiplexer_1_out, multiplexer_3_out;

  assign xnor_1_out = ~(Ra ^ R_mem);  // XNOR_Gate xnor_1, 5 bits wide
  or or_1 (or_1_out, R_mem[0], R_mem[1], R_mem[2], R_mem[3], R_mem[4]);
  assign xnor_2_out = ~(Ra ^ R_write);  // XNOR_Gate xnor_2, 5 bits wide
  or or_2 (or_2_out, R_write[0], R_write[1], R_write[2], R_write[3], R_write[4]);
  and and_1 (and_1_out, xnor_1_out[0], xnor_1_out[1], xnor_1_out[2], xnor_1_out[3], xnor_1_out[4], or_1_out);
  Multiplexer #(.width(32), .enable("false")) multiplexer_1 (
    .in0(A_value), .in1(Write_value), .out(multiplexer_1_out), .sel(and_2_out));
  and and_2 (and_2_out, xnor_2_out[0], xnor_2_out[1], xnor_2_out[2], xnor_2_out[3], xnor_2_out[4], or_2_out);
  Multiplexer #(.width(32), .enable("false")) multiplexer_2 (
    .in0(multiplexer_1_out), .in1(Mem_value), .out(resA), .sel(and_1_out));
  assign xnor_3_out = ~(Rb ^ R_mem);  // XNOR_Gate xnor_3, 5 bits wide
  or or_3 (or_3_out, R_mem[0], R_mem[1], R_mem[2], R_mem[3], R_mem[4]);
  assign xnor_4_out = ~(Rb ^ R_write);  // XNOR_Gate xnor_4, 5 bits wide
  or or_4 (or_4_out, R_write[0], R_write[1], R_write[2], R_write[3], R_write[4]);
  and and_3 (and_3_out, xnor_3_out[0], xnor_3_out[1], xnor_3_out[2], xnor_3_out[3], xnor_3_out[4], or_3_out);
  Multiplexer #(.width(32), .enable("false")) multiplexer_3 (
    .in0(B_value), .in1(Write_value), .out(multiplexer_3_out), .sel(and_4_out));
  and and_4 (and_4_out, xnor_4_out[0], xnor_4_out[1], xnor_4_out[2], xnor_4_out[3], xnor_4_out[4], or_4_out);
  Multiplexer #(.width(32), .enable("false")) multiplexer_4 (
    .in0(multiplexer_3_out), .in1(Mem_value), .out(resB), .sel(and_3_out));
endmodule

module secondBit (
  input  [3:0] inp,
  input  I_or_R,
  output res
);

  wire and_1_out, and_2_out, nor_1_out, not_1_out, or_1_out;

  not not_1 (not_1_out, inp[1]);
  nor nor_1 (nor_1_out, inp[0], inp[1], inp[2]);
  and and_1 (and_1_out, inp[0], not_1_out, inp[2]);
  or or_1 (or_1_out, and_1_out, and_2_out);
  and and_2 (and_2_out, nor_1_out, I_or_R);
  and and_3 (res, inp[3], or_1_out);
endmodule
